# Fritzing sketch Growmato (saved by Fritzing 0.9.6b)
perfboards: 1

parts:
  Part1 = Arduino Nano (Rev3.0) (ICSP)
  J1 = female pin header, 4 pins [form="♀ (female)"]
  J2 = female pin header, 4 pins [form="♀ (female)"]
  J3 = female pin header, 4 pins [form="♀ (female)"]
  J4 = female pin header, 4 pins [form="♀ (female)"]
  J5 = female pin header, 4 pins [form="♀ (female)"]
  Espessif_Serial_Wifi_Modul_1 = ESP8266 ESP01 [part_number=ESP8266 package=THT]
  IC2 = V_REG_LD1117VXX [package=78xxl]
  IC1 = Voltage Regulator [package=78xxl]
  C1 = Electrolytic Capacitor [capacitance=100µF voltage=35V package="200 mil [THT, electrolytic]"]

nets:
  GND: Part1.GND, J1.pin1, J2.pin1, J3.pin1, J4.pin1, J5.pin1, Espessif_Serial_Wifi_Modul_1.GND, IC1.GND
  N1: Part1.D8, J1.pin4
  N2: Part1.D9, J1.pin3
  N3: Part1.D10, J1.pin2
  N4: Part1.VIN, IC1.IN
  N5: Part1.5V, J2.pin2, J3.pin2, J4.pin2, J5.pin2
  N6: Part1.A5, J2.pin4, J3.pin4, J4.pin4, J5.pin4, Espessif_Serial_Wifi_Modul_1.GPIO02
  N7: Part1.A4, J2.pin3, J3.pin3, J4.pin3, J5.pin3, Espessif_Serial_Wifi_Modul_1.GPIO00
  N8: Espessif_Serial_Wifi_Modul_1.VCC, Espessif_Serial_Wifi_Modul_1.CH_PD, IC1.OUT
  N9: IC2.GND, C1.-

notes:
  9v in
  LED Port
  ESP8266 Port
  LCD Port
  SHT30 Port
  StemmaSoil Port

custom parts:
  ESP8266 ESP01: Generic WiFi Module based on the ESP8266 with onboard PCB antenna and UART communications
